// Logisim project SAMAB.circ as structural Verilog
module ALU (
  input  [15:0] Op1,
  input  [15:0] ALU_Output,
  input  [15:0] Op2,
  input  [2:0] SEL
);

  wire [15:0] adder_1_out, and_1_out, divider_1_out, multiplier_1_out, nand_1_out, or_1_out,
       subtractor_1_out, xor_1_out;

  assign and_1_out = Op1 & Op2;  // AND_Gate and_1, 16 bits wide
  assign or_1_out = Op1 | Op2;  // OR_Gate or_1, 16 bits wide
  assign xor_1_out = Op1 ^ Op2;  // XOR_Gate xor_1, 16 bits wide
  Adder #(.width(16)) adder_1 (.a(Op1), .b(Op2), .out(adder_1_out));  // open: cin, cout
  Subtractor #(.width(16)) subtractor_1 (.a(Op1), .b(Op2), .out(subtractor_1_out));  // open: bin, bout
  Multiplier #(.width(16)) multiplier_1 (.a(Op1), .b(Op2), .out(multiplier_1_out));  // open: cin, cout
  Divider #(.width(16)) divider_1 (.a(Op1), .b(Op2), .out(divider_1_out));  // open: upper, rem
  assign nand_1_out = ~(Op1 & Op2);  // NAND_Gate nand_1, 16 bits wide
  Multiplexer #(.select(3), .width(16), .enable("false")) multiplexer_1 (
    .in0(adder_1_out), .in1(subtractor_1_out), .in2(multiplier_1_out), .in3(divider_1_out), .in4(and_1_out),
    .in5(or_1_out), .in6(xor_1_out), .in7(nand_1_out), .out(ALU_Output), .sel(SEL));
endmodule
